// Logisim project 8051.circ as structural Verilog
module REGISTERS (
  input  Overflow_flag,
  input  Auxiliary_carry_flag,
  input  Carry_flag,
  input  in_4,
  input  in_5,
  input  in_6,
  input  [3:0] OPCode,
  input  Enable_write,
  input  Enable_output,
  input  [7:0] Data_input
);

  wire clock_1_out, clock_2_out, PSW_dout, undriven;
  wire [1:0] bitadder_1_out, multiplexer_3_out;
  wire [2:0] adder_1_out, counter_1_q, register_1_q;
  wire [6:0] multiplexer_2_out, register_2_q, register_3_q, register_4_q, register_5_q;
  wire [7:0] Internal_memory_dout;

  Clock clock_1 (.out(clock_1_out));
  Register #(.width(3)) register_1 (.D(adder_1_out), .clk(clock_1_out), .Q(register_1_q));  // open: en, clr
  Adder #(.width(3)) adder_1 (.out(adder_1_out), .cin(1'b1));  // open: a, b, cout
  Clock clock_2 (.out(clock_2_out));
  Register #(.width(7)) register_2 (.Q(register_2_q));  // open: D, en, clk, clr
  Register #(.width(7)) register_3 (.Q(register_3_q));  // open: D, en, clk, clr
  Register #(.width(7)) register_4 (.Q(register_4_q));  // open: D, en, clk, clr
  Register #(.width(7)) register_5 (.Q(register_5_q));  // open: D, en, clk, clr
  Multiplexer #(.select(3)) multiplexer_1 (
    .in4(Overflow_flag), .in6(Auxiliary_carry_flag), .in7(Carry_flag));  // open: in0, in1, in2, in3, in5, out, sel
  Counter #(.max('h7), .width(3)) counter_1 (
    .up(1'b1), .clk(clock_2_out), .Q(counter_1_q));  // open: clr, load, count, D, carry
  Multiplexer #(.select(2), .width(7)) multiplexer_2 (
    .in0(register_2_q), .in1(register_3_q), .in2(register_4_q), .in3(register_5_q), .out(multiplexer_2_out));  // open: sel
  BitAdder #(.width(1)) bitadder_1 (.in0(in_4), .in1(in_5), .in2(in_6), .out(bitadder_1_out));
  Multiplexer #(.select(4), .width(2)) multiplexer_3 (
    .in2(bitadder_1_out), .in3(bitadder_1_out), .in4(bitadder_1_out), .out(multiplexer_3_out), .sel(OPCode));  // open: in0, in1, in5, in6, in7, in8, in9, in10, in11, in12, in13, in14, in15
  RAM #(.addrWidth(3), .dataWidth(1)) PSW (
    .addr(counter_1_q), .we(1'b1), .clk(clock_2_out), .din(undriven), .dout(PSW_dout));  // open: oe
  RAM #(.addrWidth(7)) Internal_memory (
    .we(Enable_write), .oe(Enable_output), .din(Data_input), .dout(Internal_memory_dout));  // open: addr, clk
  // Probe on PSW_dout
  // Probe on Internal_memory_dout
  RAM #(.addrWidth(7)) SFR ();  // open: addr, we, oe, clk, din, dout

  // Notes on the sheet:
  //   IRAM (0x00 to 0xFF), where:
  //   0x20 to 0x2F - bit registers
  //   0x30 to 0x7F - non SFR registers
  //   0x80 to 0xFF - Special functions registers
  //   0x00 to 0x1F - R0 to R7 (4 banks each, 1 bank every 8 bits)
endmodule

module SFR (
  input  Clock,
  input  Overflow_flag,
  input  Auxiliary_carry_flag,
  input  Carry_flag,
  input  [3:0] OPCode
);

  wire [2:2] register_1_q_3;
  wire [5:0] register_1_q_2;
  wire [6:6] register_1_q_4;
  wire [7:0] demultiplexer_1_out2, multiplexer_1_out, multiplexer_2_out, ram_1_dout;
  wire [7:7] register_1_q;

  Register register_1 (
    .D(demultiplexer_1_out2), .clk(Clock),
    .Q({register_1_q[7], register_1_q_4[6], register_1_q_2[5:3], register_1_q_3[2], register_1_q_2[1:0]}));  // open: en, clr
  Multiplexer #(.select(4), .width(8)) multiplexer_1 (
    .in2({Carry_flag, Auxiliary_carry_flag, register_1_q_2[5:3], Overflow_flag, register_1_q_2[1:0]}),
    .in3({Carry_flag, Auxiliary_carry_flag, register_1_q_2[5:3], Overflow_flag, register_1_q_2[1:0]}),
    .in4({Carry_flag, Auxiliary_carry_flag, register_1_q_2[5:3], Overflow_flag, register_1_q_2[1:0]}),
    .in5({Carry_flag, register_1_q_4[6], register_1_q_2[5:3], Overflow_flag, register_1_q_2[1:0]}),
    .in6({Carry_flag, register_1_q_4[6], register_1_q_2[5:3], Overflow_flag, register_1_q_2[1:0]}),
    .in7({Carry_flag, register_1_q_4[6], register_1_q_2[5:3], register_1_q_3[2], register_1_q_2[1:0]}),
    .in8({Carry_flag, register_1_q_4[6], register_1_q_2[5:3], register_1_q_3[2], register_1_q_2[1:0]}),
    .out(multiplexer_1_out), .sel(OPCode));  // open: in0, in1, in9, in10, in11, in12, in13, in14, in15
  Multiplexer #(.select(4), .width(8)) multiplexer_2 (
    .in2(8'hd0), .in3(8'hd0), .in4(8'hd0), .in5(8'hd0), .in6(8'hd0), .in7(8'hd0), .in8(8'hd0),
    .out(multiplexer_2_out), .sel(OPCode));  // open: in0, in1, in9, in10, in11, in12, in13, in14, in15
  RAM ram_1 (.addr(multiplexer_2_out), .clk(Clock), .din(multiplexer_1_out), .dout(ram_1_dout));  // open: we, oe
  Demultiplexer #(.select(4), .width(8)) demultiplexer_1 (
    .out2(demultiplexer_1_out2), .out3(demultiplexer_1_out2), .out4(demultiplexer_1_out2),
    .out5(demultiplexer_1_out2), .out6(demultiplexer_1_out2), .out7(demultiplexer_1_out2),
    .out8(demultiplexer_1_out2), .in(ram_1_dout), .sel(OPCode));  // open: out0, out1, out9, out10, out11, out12, out13, out14, out15
endmodule
